# Fritzing sketch schema (saved by Fritzing 0.9.5d)
breadboards: 1

parts:
  Ардуино = Arduino Uno (Rev3)
  J1 = Basic Servo
  J2 = Basic Servo
  J3 = Basic Servo
  J4 = Basic Servo
  Joystick_KY-1 = Joystick KY-023
  Joystick_KY-2 = Joystick KY-023

nets:
  N1: Ардуино.A0, Joystick_KY-1.pin3
  N2: Ардуино.A1, Joystick_KY-1.pin4
  N3: Ардуино.A2, Joystick_KY-2.pin3
  N4: Ардуино.A3, Joystick_KY-2.pin4
  N5: Ардуино.D9_PWM, J1.pulse
  N6: Ардуино.D10_PWM/SS, J2.pulse
  N7: Ардуино.D11_PWM/MOSI, J3.pulse
  GND: Ардуино.GND, J1.gnd, J2.gnd, J3.gnd, J4.gnd, Joystick_KY-1.pin1, Joystick_KY-2.pin1
  N8: Ардуино.D6_PWM, J4.pulse
  VCC: Ардуино.5V, J1.vcc, J2.vcc, J3.vcc, J4.vcc, Joystick_KY-1.pin2, Joystick_KY-2.pin2
